# Fritzing sketch redlight (saved by Fritzing 0.9.3b)
breadboards: 1

parts:
  LED1 = LED - 5mm [color="Red (633nm)" package="5 mm [THT]"]
  LED2 = LED - 5mm [color="Orange (620nm)" package="5 mm [THT]"]
  LED3 = LED - 5mm [color="Green (570nm)" package="5 mm [THT]"]
  Composant1 = Arduino Uno (Rev3)
  R1 = Trimmer Potentiometer [maximum_resistance=10kΩ package=THT]
  S1 = Pushbutton [package="[THT]"]

nets:
  N1: LED1.cathode, LED2.cathode, LED3.cathode, Composant1.GND, R1.leg2
  N2: LED1.anode, Composant1.D8
  N3: LED2.anode, Composant1.D9_PWM
  N4: LED3.anode, Composant1.D10_PWM/SS
  N5: Composant1.A0, R1.wiper
  N6: Composant1.D2, S1.Pin_1, S1.Pin_2
  N7: Composant1.5V, R1.leg1, S1.Pin_3, S1.Pin_4
